# Fritzing sketch IoT_Device_PCB (saved by Fritzing 0.9.5d)
circuit board: 6.35cm x 10.16cm

parts:
  NodeMCU_ESP8266_V3 = NodeMCU v3 LoLin [part_number=ESP8266]

nets:
  N1: NodeMCU_ESP8266_V3.GND#6, NodeMCU_ESP8266_V3.GND#13, NodeMCU_ESP8266_V3.GND#33

notes:
  vcc
  gnd
  tx
  rx
  sda
  -
  +
  scl
  out
  usb-in
  LCD
  DHT
  RAIN
  GPS
  CS619 IoT Device PCB
  pps
  A0
  GND
  VU
  3V3
  D1
  D2
  D5
  D6
  D7
  D8
  do
  ao

custom parts:
  NodeMCU v3 LoLin: NodeMCU v3 LoLin NodeMCU (http://www.nodemcu.com/) is an open source IoT platform. It includes firmware (https://nodemcu-build.com/) which runs on the ESP8266 Wi-Fi SoC from Espressif Systems, and hardware which is based on the ESP-12E module. The term "NodeMCU" by default refers to the firmware rather than the dev kits. The firmware uses the Lua scripting language. It is based on the eLua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
