# Fritzing sketch IoT_Device_Schematic_Diagram (saved by Fritzing 0.9.5d)

parts:
  Part1 = u-blox NEO-6M GPS Breakout
  YL-83_-_Control_Board1 = YL-83 Rain Sensor - Control Board
  Part2 = LCD1602-I2C
  YL-83_-_Detection_Board1 = YL-83 Rain Sensor - Detection Board
  J1 = DHT22 temperature-humidity sensor [form="♂ (male)" package=THT]
  U2 = LIPO-2000mAh [package=lipo-2000]  # not connected
  NodeMCU_v1 = NodeMCU v3 LoLin [part_number=ESP8266]

nets:
  GND: Part1.GND, YL-83_-_Control_Board1.GND, J1.GND, NodeMCU_v1.GND#6, NodeMCU_v1.GND#13, NodeMCU_v1.GND#16, NodeMCU_v1.GND#33
  VCC: Part1.VCC, YL-83_-_Control_Board1.VCC, J1.VCC, NodeMCU_v1.3V3
  N1: Part1.TXD, NodeMCU_v1.D7
  N2: Part1.RXD, NodeMCU_v1.D8
  N3: YL-83_-_Control_Board1.DO, NodeMCU_v1.D6
  N4: YL-83_-_Control_Board1.AO, NodeMCU_v1.A0
  N5: YL-83_-_Control_Board1.POS, YL-83_-_Detection_Board1.NEG
  N6: YL-83_-_Control_Board1.NEG, YL-83_-_Detection_Board1.POS
  N7: Part2.GND, NodeMCU_v1.GND#41
  N8: Part2.VCC, NodeMCU_v1.VU
  N9: Part2.SDA, NodeMCU_v1.D2
  N10: Part2.SCL, NodeMCU_v1.D1
  N11: J1.OUT, NodeMCU_v1.D5

notes:
  Rain Drop Sensor
  DHT22
  16x2 I2C LCD
  Ublox Neo 6m GPS
  NodeMCU ESP8266
  POWER SOURCE 3.7V:
  This can be either of the following ,
  1) Li-Po Battery with micro-USB connector
  2) Micro-USB Charger
  3) Micro-USB Power Bank
  4) Micro-USB Cable connected to PC

custom parts:
  YL-83 Rain Sensor - Control Board: The YL-83 is a rain sensor that has more resistance when dry and less resistance when wet. The module runs at 5V.
  LCD1602-I2C: A standard character display, usually with 2x16 characters. Comes in many colors with LCM1602 IIC attached.
  YL-83 Rain Sensor - Detection Board: The YL-83 is a rain sensor that has more resistance when dry and less resistance when wet. The module runs at 5V.
  DHT22 temperature-humidity sensor: The DHT22 is a basic, low-cost digital temperature and humidity sensor. It uses a capacitive humidity sensor and a thermistor to measure the surrounding air, and spits out a digital signal on the data pin (no analog input pins needed). It's fairly simple to use, but requires careful timing to grab data. The only real downside of this sensor is you can only get new data from it once every 2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
  NodeMCU v3 LoLin: NodeMCU v3 LoLin NodeMCU (http://www.nodemcu.com/) is an open source IoT platform. It includes firmware (https://nodemcu-build.com/) which runs on the ESP8266 Wi-Fi SoC from Espressif Systems, and hardware which is based on the ESP-12E module. The term "NodeMCU" by default refers to the firmware rather than the dev kits. The firmware uses the Lua scripting language. It is based on the eLua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
